# Fritzing sketch circuito (saved by Fritzing 0.9.3b)
breadboards: 2

parts:
  Componente1 = Arduino Uno (Rev3)
  hc-sr1 = hc-sr04
  U2 = TOUCH [package=touch1]
  Part1 = KY-002 Vibration Switch Module [package="Breakout board"]
  R3 = Resistor [tolerance=±5% resistance=220 package=THT]
  ZS-042_RTC1 = ZS-042 RTC Module  # not connected
  R4 = Resistor [tolerance=±5% resistance=220 package=THT]
  R6 = Resistor [tolerance=±5% resistance=220 package=THT]
  Part2 = KY-011 Two Color LED Module [package="Breakout board"]

nets:
  N1: Componente1.A0, U2.T1, R3.Pin_0
  N2: Componente1.D10_PWM/SS, R6.Pin_1
  N3: Componente1.D12/MISO, R4.Pin_1
  N4: Componente1.D2, Part1.-
  N5: Componente1.D4, hc-sr1.Trig
  N6: Componente1.D6_PWM, hc-sr1.Echo
  5V: Componente1.5V, hc-sr1.VCC, Part1.Vin
  GND: Componente1.GND, hc-sr1.GND, U2.T2, Part1.S, R3.Pin_1, Part2.S
  N7: R4.Pin_0, Part2.-
  N8: R6.Pin_0, Part2.Vin

custom parts:
  KY-002 Vibration Switch Module: Arduino Vibration Switch Module KY-002 Keyes allows detection of shock and vibration.
  KY-011 Two Color LED Module: KEYES KY-011 Two Color LED Module consist of a common cathode 3mm red/green LED.
