# Fritzing sketch circuito_piezoeletrico (saved by Fritzing 0.9.3b)
breadboards: 1

parts:
  Componente1 = Arduino Uno (Rev3)
  J1 = Piezo Speaker
  R1 = Resistor [tolerance=±5% resistance=220 package=THT]
  LED1 = LED - 5mm [color="Red (633nm)" package="5 mm [THT]"]

nets:
  N1: Componente1.A0, J1.pin2, R1.Pin_0
  N2: Componente1.D11_PWM/MOSI, LED1.anode
  N3: Componente1.GND, J1.pin1, R1.Pin_1, LED1.cathode
