# Fritzing sketch projeto (saved by Fritzing 0.9.3b)
breadboards: 1

parts:
  Componente1 = Arduino Uno (Rev3)
  Part1 = KY-002 Vibration Switch Module [package="Breakout board"]
  J1 = Piezo Speaker
  hc-sr1 = hc-sr04
  LED1 = LED - 5mm [color="Red (633nm)" package="5 mm [THT]"]
  LED2 = LED - 5mm [color="Yellow (585nm)" package="5 mm [THT]"]
  R1 = Resistor [tolerance=±5% resistance=220 package=THT]
  S1 = Pushbutton [package="[THT]"]
  LED4 = LED - 5mm [color="Yellow (585nm)" package="5 mm [THT]"]
  LED3 = smd LED [color="Green (555nm)" package="0603 [SMD]"]
  S2 = Pushbutton [package="[THT]"]
  R2 = Resistor [tolerance=±5% resistance=220 package=THT]
  LED5 = smd LED [color="Green (555nm)" package="0603 [SMD]"]
  R3 = Resistor [tolerance=±5% resistance=220 package=THT]

nets:
  N1: Componente1.A0, J1.pin2, R3.Pin_0
  N2: Componente1.D9_PWM, LED4.anode
  N3: Componente1.D10_PWM/SS, LED3.anode
  N4: Componente1.D11_PWM/MOSI, LED1.anode
  N5: Componente1.D12/MISO, LED2.anode
  N6: Componente1.D13/SCK, LED5.anode
  N7: Componente1.D3_PWM, hc-sr1.Echo
  N8: Componente1.D4, Part1.S
  N9: Componente1.D5_PWM, R1.Pin_0, S1.Pin_1, S1.Pin_2
  N10: Componente1.D6_PWM, S2.Pin_3, S2.Pin_4, R2.Pin_0
  5V: Componente1.5V, Part1.Vin, hc-sr1.VCC, R1.Pin_1, R2.Pin_1
  GND: Componente1.GND, Part1.-, J1.pin1, hc-sr1.GND, LED1.cathode, LED2.cathode, S1.Pin_3, S1.Pin_4, LED4.cathode, LED3.cathode, S2.Pin_1, S2.Pin_2, LED5.cathode, R3.Pin_1

custom parts:
  KY-002 Vibration Switch Module: Arduino Vibration Switch Module KY-002 Keyes allows detection of shock and vibration.
