# Fritzing sketch circuito_relogio_binario (saved by Fritzing 0.9.3b)
breadboards: 2

parts:
  Componente1 = Arduino Uno (Rev3)
  ZS-042_RTC1 = ZS-042 RTC Module  # not connected
  LED1 = LED - 5mm [color="Red (633nm)" package="5 mm [THT]"]
  LED2 = LED - 5mm [color="Red (633nm)" package="5 mm [THT]"]
  LED3 = LED - 5mm [color="Red (633nm)" package="5 mm [THT]"]
  LED4 = LED - 5mm [color="Red (633nm)" package="5 mm [THT]"]
  LED5 = LED - 5mm [color="Red (633nm)" package="5 mm [THT]"]
  LED6 = LED - 5mm [color="Red (633nm)" package="5 mm [THT]"]
  LED7 = LED - 5mm [color="Green (555nm)" package="5 mm [THT]"]
  LED8 = LED - 5mm [color="Green (555nm)" package="5 mm [THT]"]
  LED9 = LED - 5mm [color="Green (555nm)" package="5 mm [THT]"]
  LED10 = LED - 5mm [color="Green (555nm)" package="5 mm [THT]"]

nets:
  N1: Componente1.D8, LED4.anode
  N2: Componente1.D9_PWM, LED3.anode
  N3: Componente1.D10_PWM/SS, LED2.anode
  N4: Componente1.D11_PWM/MOSI, LED1.anode
  N5: Componente1.GND, LED1.cathode, LED2.cathode, LED3.cathode, LED4.cathode, LED5.cathode, LED6.cathode, LED7.cathode, LED8.cathode, LED9.cathode, LED10.cathode
  N6: Componente1.D2, LED7.anode
  N7: Componente1.D3_PWM, LED8.anode
  N8: Componente1.D4, LED9.anode
  N9: Componente1.D5_PWM, LED10.anode
  N10: Componente1.D6_PWM, LED6.anode
  N11: Componente1.D7, LED5.anode
