# Fritzing sketch circuito_ultrasonico (saved by Fritzing 0.9.3b)
breadboards: 1

parts:
  Componente1 = Arduino Uno (Rev3)
  hc-sr1 = hc-sr04
  LED1 = smd LED [color="Red (633nm)" package="0805 [SMD]"]

nets:
  N1: Componente1.D11_PWM/MOSI, LED1.anode
  GND: Componente1.GND, hc-sr1.GND, LED1.cathode
  N2: Componente1.D2, hc-sr1.Trig
  N3: Componente1.D4, hc-sr1.Echo
  5V: Componente1.5V, hc-sr1.VCC
