# Fritzing sketch circuito_vibracao (saved by Fritzing 0.9.3b)
breadboards: 1

parts:
  Componente2 = Arduino Uno (Rev3)
  LED2 = smd LED [color="Red (633nm)" package="0805 [SMD]"]
  Part1 = KY-002 Vibration Switch Module [package="Breakout board"]

nets:
  N1: Componente2.D11_PWM/MOSI, LED2.anode
  N2: Componente2.GND, LED2.cathode, Part1.-
  N3: Componente2.D4, Part1.S
  5V: Componente2.5V, Part1.Vin

custom parts:
  KY-002 Vibration Switch Module: Arduino Vibration Switch Module KY-002 Keyes allows detection of shock and vibration.
